// Logisim project main.circ as structural Verilog: 8 circuits, main circuit main
module main (
);

  wire clock_1_out;
  wire [31:0] fetch_sub_1_out, if_id_pipeline_register_1_instruction_2, if_id_pipeline_register_1_pc_4_2,
       mipsprogramrom_1_p2;

  Clock clock_1 (.out(clock_1_out));
  Fetch_Sub fetch_sub_1 (.Clock(clock_1_out), .Out(fetch_sub_1_out));
  // MIPSProgramROM mipsprogramrom_1: pin names not known; wires that end beside it: fetch_sub_1_out, mipsprogramrom_1_p2
  IF_ID_Pipeline_Register if_id_pipeline_register_1 (
    .PC_4(fetch_sub_1_out), .Instruction(mipsprogramrom_1_p2), .Clock(clock_1_out),
    .PC_4_2(if_id_pipeline_register_1_pc_4_2), .Instruction_2(if_id_pipeline_register_1_instruction_2));
  // RegisterFile registerfile_1: pin names not known; wires that end beside it: if_id_pipeline_register_1_instruction_2[25:21], if_id_pipeline_register_1_instruction_2[20:16]
endmodule

module PC_Inc (
  input  [31:0] Input,
  output [31:0] Output
);

  // Incrementer incrementer_1: pin names not known; wires that end beside it: Input[31:2], Output[31:2]

  assign Output[1:0] = Input[1:0];
endmodule

// PC+4
module Fetch_Sub (
  input  Clock,
  output [31:0] Out
);

  wire [31:0] pc_inc_1_output;

  Register #(.width(32)) register_1 (.D(pc_inc_1_output), .Q(Out), .clk(Clock));  // open: en, clr
  PC_Inc pc_inc_1 (.Input(Out), .Output(pc_inc_1_output));
endmodule

// IF/ID
module IF_ID_Pipeline_Register (
  input  [31:0] PC_4,
  input  [31:0] Instruction,
  input  Clock,
  output [31:0] PC_4_2,
  output [31:0] Instruction_2
);

  Register #(.width(32)) u_PC_4 (.D(PC_4), .Q(PC_4_2), .clk(Clock));  // open: en, clr
  Register #(.width(32)) u_Instruction (.D(Instruction), .Q(Instruction_2), .clk(Clock));  // open: en, clr
endmodule

module OpCtrl (
  input  Op5,
  input  Op4,
  input  Op3,
  input  Op2,
  input  Op1,
  input  Op0,
  output RegDst,
  output Branch,
  output MemRead,
  output MemToReg,
  output MemWrite,
  output ALUsr,
  output RegWrite,
  output Special,
  output RegIn
);

  wire and_2_out, and_3_out, and_4_out, and_5_out, and_6_out, and_7_out, and_8_out, and_9_out, and_10_out,
       and_11_out, and_12_out, and_13_out, and_14_out, and_15_out, and_16_out, and_17_out, and_18_out,
       and_19_out, and_20_out, not_1_out, not_2_out, not_3_out, not_4_out, not_5_out, not_6_out, not_7_out,
       not_8_out, not_9_out, not_10_out, not_11_out, not_12_out, not_13_out, not_14_out, not_15_out,
       not_16_out, not_17_out, not_18_out, not_19_out, not_20_out, not_21_out, not_22_out, not_23_out,
       not_24_out, not_25_out, not_26_out, not_27_out, not_28_out, not_29_out, not_30_out, not_31_out,
       not_32_out, not_33_out, not_34_out, not_35_out, not_36_out, not_37_out, not_38_out, not_39_out,
       not_40_out, not_41_out, not_42_out, not_43_out, not_44_out, not_45_out, not_46_out, not_47_out,
       not_48_out, not_49_out, not_50_out, not_51_out, not_52_out, not_53_out, not_54_out, not_55_out,
       not_56_out, not_57_out, not_58_out, not_59_out, not_60_out, not_61_out, not_62_out, not_63_out,
       not_64_out, not_65_out, not_66_out, not_67_out, not_68_out, not_69_out;

  not not_1 (not_1_out, Op5);
  not not_2 (not_2_out, Op4);
  not not_3 (not_3_out, Op3);
  not not_4 (not_4_out, Op5);
  not not_5 (not_5_out, Op4);
  not not_6 (not_6_out, Op3);
  not not_7 (not_7_out, Op5);
  not not_8 (not_8_out, Op4);
  not not_9 (not_9_out, Op3);
  not not_10 (not_10_out, Op4);
  not not_11 (not_11_out, Op3);
  not not_12 (not_12_out, Op1);
  not not_13 (not_13_out, Op0);
  not not_14 (not_14_out, Op4);
  not not_15 (not_15_out, Op3);
  not not_16 (not_16_out, Op2);
  not not_17 (not_17_out, Op4);
  not not_18 (not_18_out, Op3);
  not not_19 (not_19_out, Op1);
  not not_20 (not_20_out, Op0);
  not not_21 (not_21_out, Op4);
  not not_22 (not_22_out, Op3);
  not not_23 (not_23_out, Op2);
  not not_24 (not_24_out, Op4);
  not not_25 (not_25_out, Op2);
  not not_26 (not_26_out, Op1);
  not not_27 (not_27_out, Op0);
  not not_28 (not_28_out, Op4);
  not not_29 (not_29_out, Op2);
  not not_30 (not_30_out, Op5);
  not not_31 (not_31_out, Op4);
  not not_32 (not_32_out, Op5);
  not not_33 (not_33_out, Op4);
  not not_34 (not_34_out, Op5);
  not not_35 (not_35_out, Op4);
  not not_36 (not_36_out, Op4);
  not not_37 (not_37_out, Op3);
  not not_38 (not_38_out, Op1);
  not not_39 (not_39_out, Op0);
  not not_40 (not_40_out, Op4);
  not not_41 (not_41_out, Op2);
  not not_42 (not_42_out, Op1);
  not not_43 (not_43_out, Op0);
  not not_44 (not_44_out, Op4);
  not not_45 (not_45_out, Op2);
  not not_46 (not_46_out, Op4);
  not not_47 (not_47_out, Op3);
  not not_48 (not_48_out, Op2);
  not not_49 (not_49_out, Op5);
  not not_50 (not_50_out, Op4);
  not not_51 (not_51_out, Op5);
  not not_52 (not_52_out, Op4);
  not not_53 (not_53_out, Op5);
  not not_54 (not_54_out, Op4);
  not not_55 (not_55_out, Op4);
  not not_56 (not_56_out, Op3);
  not not_57 (not_57_out, Op1);
  not not_58 (not_58_out, Op0);
  not not_59 (not_59_out, Op5);
  not not_60 (not_60_out, Op4);
  not not_61 (not_61_out, Op3);
  not not_62 (not_62_out, Op2);
  not not_63 (not_63_out, Op1);
  not not_64 (not_64_out, Op0);
  not not_65 (not_65_out, Op5);
  not not_66 (not_66_out, Op4);
  not not_67 (not_67_out, Op3);
  not not_68 (not_68_out, Op2);
  not not_69 (not_69_out, Op1);
  and and_1 (RegDst, not_1_out, not_2_out, not_3_out, Op2);
  and and_2 (and_2_out, not_4_out, not_5_out, not_6_out, Op1);
  and and_3 (and_3_out, not_7_out, not_8_out, not_9_out, Op2);
  and and_4 (and_4_out, Op5, not_10_out, not_11_out, not_12_out, not_13_out);
  and and_5 (and_5_out, Op5, not_14_out, not_15_out, not_16_out, Op1, Op0);
  and and_6 (and_6_out, Op5, not_17_out, not_18_out, not_19_out, not_20_out);
  and and_7 (and_7_out, Op5, not_21_out, not_22_out, not_23_out, Op1, Op0);
  and and_8 (and_8_out, Op5, not_24_out, Op3, not_25_out, not_26_out, not_27_out);
  and and_9 (and_9_out, Op5, not_28_out, Op3, not_29_out, Op1, Op0);
  and and_10 (and_10_out, not_30_out, not_31_out, Op3, Op0);
  and and_11 (and_11_out, not_32_out, not_33_out, Op3, Op1);
  and and_12 (and_12_out, not_34_out, not_35_out, Op3, Op2);
  and and_13 (and_13_out, Op5, not_36_out, not_37_out, not_38_out, not_39_out);
  and and_14 (and_14_out, Op5, not_40_out, not_41_out, not_42_out, not_43_out);
  and and_15 (and_15_out, Op5, not_44_out, not_45_out, Op1, Op0);
  and and_16 (and_16_out, not_46_out, not_47_out, not_48_out, Op1, Op0);
  and and_17 (and_17_out, not_49_out, not_50_out, Op3, Op0);
  and and_18 (and_18_out, not_51_out, not_52_out, Op3, Op1);
  and and_19 (and_19_out, not_53_out, not_54_out, Op3, Op2);
  and and_20 (and_20_out, Op5, not_55_out, not_56_out, not_57_out, not_58_out);
  and and_21 (Special, not_59_out, not_60_out, not_61_out, not_62_out, not_63_out, not_64_out);
  and and_22 (RegIn, not_65_out, not_66_out, not_67_out, not_68_out, not_69_out, Op0);
  or or_1 (Branch, and_2_out, and_3_out);
  or or_2 (MemRead, and_4_out, and_5_out);
  or or_3 (MemToReg, and_6_out, and_7_out);
  or or_4 (MemWrite, and_8_out, and_9_out);
  or or_5 (ALUsr, and_10_out, and_11_out, and_12_out, and_13_out, and_14_out, and_15_out);
  or or_6 (RegWrite, and_16_out, and_17_out, and_18_out, and_19_out, and_20_out);
endmodule

module Special_Ctrl (
  input  Func5,
  input  Func4,
  input  Func3,
  input  Func2,
  input  Func1,
  input  Func0,
  output RegDST,
  output Branch,
  output ALUsrc,
  output RegWrite,
  output Int
);

  wire and_1_out, and_2_out, and_3_out, and_4_out, and_5_out, and_7_out, and_8_out, and_9_out, and_10_out,
       and_11_out, and_12_out, and_13_out, and_14_out, and_15_out, and_16_out, not_1_out, not_2_out,
       not_3_out, not_4_out, not_5_out, not_6_out, not_7_out, not_8_out, not_9_out, not_10_out, not_11_out,
       not_12_out, not_13_out, not_14_out, not_15_out, not_16_out, not_17_out, not_18_out, not_19_out,
       not_20_out, not_21_out, not_22_out, not_23_out, not_24_out, not_25_out, not_26_out, not_27_out,
       not_28_out, not_29_out, not_30_out, not_31_out, not_32_out, not_33_out, not_34_out, not_35_out,
       not_36_out, not_37_out, not_38_out, not_39_out, not_40_out, not_41_out, not_42_out, not_43_out,
       not_44_out, not_45_out, not_46_out, not_47_out, not_48_out, not_49_out;

  not not_1 (not_1_out, Func4);
  not not_2 (not_2_out, Func3);
  not not_3 (not_3_out, Func0);
  not not_4 (not_4_out, Func4);
  not not_5 (not_5_out, Func3);
  not not_6 (not_6_out, Func5);
  not not_7 (not_7_out, Func4);
  not not_8 (not_8_out, Func2);
  not not_9 (not_9_out, Func4);
  not not_10 (not_10_out, Func2);
  not not_11 (not_11_out, Func4);
  not not_12 (not_12_out, Func3);
  not not_13 (not_13_out, Func5);
  not not_14 (not_14_out, Func4);
  not not_15 (not_15_out, Func2);
  not not_16 (not_16_out, Func1);
  not not_17 (not_17_out, Func5);
  not not_18 (not_18_out, Func4);
  not not_19 (not_19_out, Func3);
  not not_20 (not_20_out, Func2);
  not not_21 (not_21_out, Func0);
  not not_22 (not_22_out, Func5);
  not not_23 (not_23_out, Func4);
  not not_24 (not_24_out, Func3);
  not not_25 (not_25_out, Func2);
  not not_26 (not_26_out, Func5);
  not not_27 (not_27_out, Func4);
  not not_28 (not_28_out, Func3);
  not not_29 (not_29_out, Func0);
  not not_30 (not_30_out, Func5);
  not not_31 (not_31_out, Func4);
  not not_32 (not_32_out, Func3);
  not not_33 (not_33_out, Func4);
  not not_34 (not_34_out, Func3);
  not not_35 (not_35_out, Func0);
  not not_36 (not_36_out, Func5);
  not not_37 (not_37_out, Func4);
  not not_38 (not_38_out, Func2);
  not not_39 (not_39_out, Func4);
  not not_40 (not_40_out, Func2);
  not not_41 (not_41_out, Func4);
  not not_42 (not_42_out, Func3);
  not not_43 (not_43_out, Func5);
  not not_44 (not_44_out, Func4);
  not not_45 (not_45_out, Func3);
  not not_46 (not_46_out, Func0);
  not not_47 (not_47_out, Func5);
  not not_48 (not_48_out, Func4);
  not not_49 (not_49_out, Func3);
  and and_1 (and_1_out, not_1_out, not_2_out, Func2, not_3_out);
  and and_2 (and_2_out, not_4_out, not_5_out, Func2, Func1);
  and and_3 (and_3_out, not_6_out, not_7_out, Func3, not_8_out, Func0);
  and and_4 (and_4_out, not_9_out, Func3, not_10_out, Func1);
  and and_5 (and_5_out, Func5, not_11_out, not_12_out, Func0);
  and and_6 (Branch, not_13_out, not_14_out, Func3, not_15_out, not_16_out);
  and and_7 (and_7_out, not_17_out, not_18_out, not_19_out, not_20_out, not_21_out);
  and and_8 (and_8_out, not_22_out, not_23_out, not_24_out, not_25_out, Func1);
  and and_9 (and_9_out, not_26_out, not_27_out, not_28_out, not_29_out);
  and and_10 (and_10_out, not_30_out, not_31_out, not_32_out, Func1);
  and and_11 (and_11_out, not_33_out, not_34_out, Func2, not_35_out);
  and and_12 (and_12_out, not_36_out, not_37_out, Func3, not_38_out, Func0);
  and and_13 (and_13_out, not_39_out, Func3, not_40_out, Func1);
  and and_14 (and_14_out, Func5, not_41_out, not_42_out, Func0);
  and and_15 (and_15_out, not_43_out, not_44_out, not_45_out, not_46_out);
  and and_16 (and_16_out, not_47_out, not_48_out, not_49_out, Func1);
  or or_1 (RegDST, and_1_out, and_2_out, and_3_out, and_4_out, and_5_out);
  or or_2 (ALUsrc, and_7_out, and_8_out);
  or or_3 (RegWrite, and_9_out, and_10_out, and_11_out, and_12_out, and_13_out, and_14_out);
  or or_4 (Int, and_15_out, and_16_out);
endmodule

module RegIn_Ctrl (
  input  rt4,
  input  rt3,
  input  rt2,
  input  rt1,
  input  rt0,
  output Brach
);

  wire not_1_out, not_2_out, not_3_out, not_4_out;

  not not_1 (not_1_out, rt4);
  not not_2 (not_2_out, rt3);
  not not_3 (not_3_out, rt2);
  not not_4 (not_4_out, rt1);
  and and_1 (Brach, not_1_out, not_2_out, not_3_out, not_4_out);
endmodule

module Control (
  input  [5:0] Op_Code,
  input  [5:0] func,
  input  [4:0] rt,
  output RegDst,
  output Branch,
  output MemRea,
  output MemRea_2,
  output MemtoReg,
  output Memwrite,
  output ALUsrc,
  output RegWrite,
  output RegWrite_2,
  output Int,
  output Int_2
);

  wire opctrl_1_regdst, opctrl_1_special, special_ctrl_1_regdst;

  OpCtrl opctrl_1 (
    .Op5(Op_Code[5]), .Op4(Op_Code[4]), .Op3(Op_Code[3]), .Op2(Op_Code[2]), .Op1(Op_Code[1]),
    .Op0(Op_Code[0]), .RegDst(opctrl_1_regdst), .Special(opctrl_1_special));  // open: Branch, MemRead, MemToReg, MemWrite, ALUsr, RegWrite, RegIn
  Special_Ctrl special_ctrl_1 (
    .Func5(func[5]), .Func4(func[4]), .Func3(func[3]), .Func2(func[2]), .Func1(func[1]), .Func0(func[0]),
    .RegDST(special_ctrl_1_regdst));  // open: Branch, ALUsrc, RegWrite, Int
  RegIn_Ctrl regin_ctrl_1 (.rt4(rt[4]), .rt3(rt[3]), .rt2(rt[2]), .rt1(rt[1]), .rt0(rt[0]));  // open: Brach
  Multiplexer multiplexer_1 (
    .in0(opctrl_1_regdst), .in1(special_ctrl_1_regdst), .out(RegDst), .sel(opctrl_1_special));  // open: en

  assign Int_2 = Int;
  assign MemRea_2 = MemRea;
  assign RegWrite_2 = RegWrite;
endmodule
